// Logisim project Passo_a_Passo_somador8BIT.circ as structural Verilog: 4 circuits, main circuit HALFADDER
module HALFADDER (
  input  A,
  input  B,
  output S,
  output C0
);

  xor xor_1 (S, A, B);
  and and_1 (C0, A, B);
endmodule

module FULLADDER (
  input  Ci,
  input  A,
  input  B,
  output S,
  output Co
);

  wire halfadder_1_c0, halfadder_1_s, halfadder_2_c0;

  HALFADDER halfadder_1 (.A(A), .B(B), .S(halfadder_1_s), .C0(halfadder_1_c0));
  HALFADDER halfadder_2 (.A(Ci), .B(halfadder_1_s), .S(S), .C0(halfadder_2_c0));
  or or_1 (Co, halfadder_2_c0, halfadder_1_c0);
endmodule

module ADDER4B (
  input  C0,
  input  A0,
  input  B0,
  input  A1,
  input  B1,
  input  A2,
  input  B2,
  input  A3,
  input  B3,
  output S0,
  output S1,
  output S2,
  output S3,
  output C4
);

  wire fulladder_1_co, fulladder_2_co, fulladder_3_co;

  FULLADDER fulladder_1 (.Ci(C0), .A(A0), .B(B0), .S(S0), .Co(fulladder_1_co));
  FULLADDER fulladder_2 (.Ci(fulladder_1_co), .A(A1), .B(B1), .S(S1), .Co(fulladder_2_co));
  FULLADDER fulladder_3 (.Ci(fulladder_2_co), .A(A2), .B(B2), .S(S2), .Co(fulladder_3_co));
  FULLADDER fulladder_4 (.Ci(fulladder_3_co), .A(A3), .B(B3), .S(S3), .Co(C4));

  // Notes on the sheet:
  //   Representação para OVERFLOW aritimético
endmodule

module ADDER8B (
  input  C0,
  input  A0,
  input  B0,
  input  A1,
  input  B1,
  input  A2,
  input  B2,
  input  A3,
  input  B3,
  input  A4,
  input  B4,
  input  A5,
  input  B5,
  input  A6,
  input  B6,
  input  A7,
  input  B7,
  output S0,
  output S1,
  output S2,
  output S3,
  output S4,
  output S5,
  output S6,
  output S7,
  output C8
);

  wire adder4b_1_c4;

  ADDER4B adder4b_1 (
    .C0(C0), .A0(A0), .B0(B0), .A1(A1), .B1(B1), .A2(A2), .B2(B2), .A3(A3), .B3(B3), .S0(S0), .S1(S1),
    .S2(S2), .S3(S3), .C4(adder4b_1_c4));
  ADDER4B adder4b_2 (
    .C0(adder4b_1_c4), .A0(A4), .B0(B4), .A1(A5), .B1(B5), .A2(A6), .B2(B6), .A3(A7), .B3(B7), .S0(S4),
    .S1(S5), .S2(S6), .S3(S7), .C4(C8));

  // Notes on the sheet:
  //   CAPTAÇÃO DO OVERFLOW POR MEIO DE UMA SAÍDA
endmodule
