// Logisim project Projeto_ULA_FINALIZADO.circ as structural Verilog: 13 circuits, main circuit DiagramaHalfAdder
module main (
  input  B7,
  input  B6,
  input  B5,
  input  B4,
  input  B3,
  input  B2,
  input  B1,
  input  B0,
  input  A7,
  input  A6,
  input  A5,
  input  A4,
  input  A3,
  input  A2,
  input  A1,
  input  A0,
  input  CRTL2,
  input  CRTL1,
  input  CRTL0,
  output out_20,
  output out_21,
  output out_22,
  output out_23,
  output out_24,
  output out_25,
  output out_26,
  output out_27
);

  wire bcd_to_7_segment_decoder_1_p1, bcd_to_7_segment_decoder_1_p2, bcd_to_7_segment_decoder_1_p3,
       bcd_to_7_segment_decoder_1_p4, bcd_to_7_segment_decoder_1_p5, bcd_to_7_segment_decoder_1_p6,
       bcd_to_7_segment_decoder_1_p7, bcd_to_7_segment_decoder_1_p8, bcd_to_7_segment_decoder_2_p1,
       bcd_to_7_segment_decoder_2_p2, bcd_to_7_segment_decoder_2_p3, bcd_to_7_segment_decoder_2_p4,
       bcd_to_7_segment_decoder_2_p6, bcd_to_7_segment_decoder_2_p7, bcd_to_7_segment_decoder_2_p8,
       bcd_to_7_segment_decoder_3_p1, bcd_to_7_segment_decoder_3_p2, bcd_to_7_segment_decoder_3_p3,
       bcd_to_7_segment_decoder_3_p4, bcd_to_7_segment_decoder_3_p6, bcd_to_7_segment_decoder_3_p7,
       bcd_to_7_segment_decoder_3_p8, binary_to_bcd_converter_1_p1, binary_to_bcd_converter_1_p3,
       binary_to_bcd_converter_1_p4, fulladder8bit_1_carry, fulladder8bit_1_overflow,
       fullsubtractor8bit_1_carry, fullsubtractor8bit_1_overflow;
  wire [7:0] and8bitwise_1_s0, fulladder8bit_1_s0, fullsubtractor8bit_1_s0, nand8bitwise_1_s0,
       nor8bitwise_1_s0, or8bitwise_1_s0, xnor8bitwise_1_s0, xor8bitwise_1_s0;

  FullAdder8bit fulladder8bit_1 (
    .A0(A0), .B0(B0), .A1(A1), .B1(B1), .A2(A2), .B2(B2), .A3(A3), .B3(B3), .A4(A4), .B4(B4), .A5(A5),
    .B5(B5), .A6(A6), .B6(B6), .A7(A7), .B7(B7), .S0(fulladder8bit_1_s0[0]), .S1(fulladder8bit_1_s0[1]),
    .S2(fulladder8bit_1_s0[2]), .S3(fulladder8bit_1_s0[3]), .S4(fulladder8bit_1_s0[4]),
    .S5(fulladder8bit_1_s0[5]), .S6(fulladder8bit_1_s0[6]), .S7(fulladder8bit_1_s0[7]),
    .Carry(fulladder8bit_1_carry), .OVERFLOW(fulladder8bit_1_overflow));
  FullSubtractor8bit fullsubtractor8bit_1 (
    .A0(A0), .B0(B0), .A1(A1), .B1(B1), .A2(A2), .B2(B2), .A3(A3), .B3(B3), .A4(A4), .B4(B4), .A5(A5),
    .B5(B5), .A6(A6), .B6(B6), .A7(A7), .B7(B7), .S0(fullsubtractor8bit_1_s0[0]),
    .S1(fullsubtractor8bit_1_s0[1]), .S2(fullsubtractor8bit_1_s0[2]), .S3(fullsubtractor8bit_1_s0[3]),
    .S4(fullsubtractor8bit_1_s0[4]), .S5(fullsubtractor8bit_1_s0[5]), .S6(fullsubtractor8bit_1_s0[6]),
    .S7(fullsubtractor8bit_1_s0[7]), .Carry(fullsubtractor8bit_1_carry),
    .OVERFLOW(fullsubtractor8bit_1_overflow));
  AND8bitWISE and8bitwise_1 (
    .A0(A0), .B0(B0), .A1(A1), .B1(B1), .A2(A2), .B2(B2), .A3(A3), .B3(B3), .A4(A4), .B4(B4), .A5(A5),
    .B5(B5), .A6(A6), .B6(B6), .A7(A7), .B7(B7), .S0(and8bitwise_1_s0[0]), .S1(and8bitwise_1_s0[1]),
    .S2(and8bitwise_1_s0[2]), .S3(and8bitwise_1_s0[3]), .S4(and8bitwise_1_s0[4]), .S5(and8bitwise_1_s0[5]),
    .S6(and8bitwise_1_s0[6]), .S7(and8bitwise_1_s0[7]));
  OR8bitWISE or8bitwise_1 (
    .A0(A0), .B0(B0), .A1(A1), .B1(B1), .A2(A2), .B2(B2), .A3(A3), .B3(B3), .A4(A4), .B4(B4), .A5(A5),
    .B5(B5), .A6(A6), .B6(B6), .A7(A7), .B7(B7), .S0(or8bitwise_1_s0[0]), .S1(or8bitwise_1_s0[1]),
    .S2(or8bitwise_1_s0[2]), .S3(or8bitwise_1_s0[3]), .S4(or8bitwise_1_s0[4]), .S5(or8bitwise_1_s0[5]),
    .S6(or8bitwise_1_s0[6]), .S7(or8bitwise_1_s0[7]));
  XOR8bitWISE xor8bitwise_1 (
    .A0(A0), .B0(B0), .A1(A1), .B1(B1), .A2(A2), .B2(B2), .A3(A3), .B3(B3), .A4(A4), .B4(B4), .A5(A5),
    .B5(B5), .A6(A6), .B6(B6), .A7(A7), .B7(B7), .S0(xor8bitwise_1_s0[0]), .S1(xor8bitwise_1_s0[1]),
    .S2(xor8bitwise_1_s0[2]), .S3(xor8bitwise_1_s0[3]), .S4(xor8bitwise_1_s0[4]), .S5(xor8bitwise_1_s0[5]),
    .S6(xor8bitwise_1_s0[6]), .S7(xor8bitwise_1_s0[7]));
  NAND8bitWISE nand8bitwise_1 (
    .A0(A0), .B0(B0), .A1(A1), .B1(B1), .A2(A2), .B2(B2), .A3(A3), .B3(B3), .A4(A4), .B4(B4), .A5(A5),
    .B5(B5), .A6(A6), .B6(B6), .A7(A7), .B7(B7), .S0(nand8bitwise_1_s0[0]), .S1(nand8bitwise_1_s0[1]),
    .S2(nand8bitwise_1_s0[2]), .S3(nand8bitwise_1_s0[3]), .S4(nand8bitwise_1_s0[4]),
    .S5(nand8bitwise_1_s0[5]), .S6(nand8bitwise_1_s0[6]), .S7(nand8bitwise_1_s0[7]));
  NOR8bitWISE nor8bitwise_1 (
    .A0(A0), .B0(B0), .A1(A1), .B1(B1), .A2(A2), .B2(B2), .A3(A3), .B3(B3), .A4(A4), .B4(B4), .A5(A5),
    .B5(B5), .A6(A6), .B6(B6), .A7(A7), .B7(B7), .S0(nor8bitwise_1_s0[0]), .S1(nor8bitwise_1_s0[1]),
    .S2(nor8bitwise_1_s0[2]), .S3(nor8bitwise_1_s0[3]), .S4(nor8bitwise_1_s0[4]), .S5(nor8bitwise_1_s0[5]),
    .S6(nor8bitwise_1_s0[6]), .S7(nor8bitwise_1_s0[7]));
  XNOR8bitWISE xnor8bitwise_1 (
    .A0(A0), .B0(B0), .A1(A1), .B1(B1), .A2(A2), .B2(B2), .A3(A3), .B3(B3), .A4(A4), .B4(B4), .A5(A5),
    .B5(B5), .A6(A6), .B6(B6), .A7(A7), .B7(B7), .S0(xnor8bitwise_1_s0[0]), .S1(xnor8bitwise_1_s0[1]),
    .S2(xnor8bitwise_1_s0[2]), .S3(xnor8bitwise_1_s0[3]), .S4(xnor8bitwise_1_s0[4]),
    .S5(xnor8bitwise_1_s0[5]), .S6(xnor8bitwise_1_s0[6]), .S7(xnor8bitwise_1_s0[7]));
  LED UsignedOVERFLOW (.in(fulladder8bit_1_carry));
  LED subPOSITIVA (.in(fullsubtractor8bit_1_carry));
  LED #(.active("false")) subNEGATIVA (.in(fullsubtractor8bit_1_carry));
  LED OVERFLOW (.in(fulladder8bit_1_overflow));
  LED led_1 (.in(fullsubtractor8bit_1_overflow));
  Multiplexer #(.select(3), .width(8)) multiplexer_1 (
    .in0(fulladder8bit_1_s0), .in1(fullsubtractor8bit_1_s0), .in2(and8bitwise_1_s0), .in3(or8bitwise_1_s0),
    .in4(xor8bitwise_1_s0), .in5(nand8bitwise_1_s0), .in6(nor8bitwise_1_s0), .in7(xnor8bitwise_1_s0),
    .out({out_27, out_26, out_25, out_24, out_23, out_22, out_21, out_20}), .sel({CRTL2, CRTL1, CRTL0}));
  _7_Segment_Display u_7_segment_display_1 (
    .g(bcd_to_7_segment_decoder_1_p1), .f(bcd_to_7_segment_decoder_1_p3), .a(bcd_to_7_segment_decoder_1_p6),
    .b(bcd_to_7_segment_decoder_1_p8), .e(bcd_to_7_segment_decoder_1_p2), .d(bcd_to_7_segment_decoder_1_p4),
    .c(bcd_to_7_segment_decoder_1_p7));  // open: dp
  // BCD_to_7_Segment_decoder bcd_to_7_segment_decoder_1: pin names not known; wires that end beside it: bcd_to_7_segment_decoder_1_p1, bcd_to_7_segment_decoder_1_p2, bcd_to_7_segment_decoder_1_p3, bcd_to_7_segment_decoder_1_p4, bcd_to_7_segment_decoder_1_p5, bcd_to_7_segment_decoder_1_p6, bcd_to_7_segment_decoder_1_p7, bcd_to_7_segment_decoder_1_p8
  // Binary_to_BCD_converter #(.binvalue(8)) binary_to_bcd_converter_1: pin names not known; wires that end beside it: binary_to_bcd_converter_1_p1, bcd_to_7_segment_decoder_1_p5, binary_to_bcd_converter_1_p3, binary_to_bcd_converter_1_p4
  _7_Segment_Display u_7_segment_display_2 (
    .g(bcd_to_7_segment_decoder_2_p1), .f(bcd_to_7_segment_decoder_2_p3), .a(bcd_to_7_segment_decoder_2_p6),
    .b(bcd_to_7_segment_decoder_2_p8), .e(bcd_to_7_segment_decoder_2_p2), .d(bcd_to_7_segment_decoder_2_p4),
    .c(bcd_to_7_segment_decoder_2_p7));  // open: dp
  // BCD_to_7_Segment_decoder bcd_to_7_segment_decoder_2: pin names not known; wires that end beside it: bcd_to_7_segment_decoder_2_p1, bcd_to_7_segment_decoder_2_p2, bcd_to_7_segment_decoder_2_p3, bcd_to_7_segment_decoder_2_p4, binary_to_bcd_converter_1_p3, bcd_to_7_segment_decoder_2_p6, bcd_to_7_segment_decoder_2_p7, bcd_to_7_segment_decoder_2_p8
  _7_Segment_Display u_7_segment_display_3 (
    .g(bcd_to_7_segment_decoder_3_p1), .f(bcd_to_7_segment_decoder_3_p3), .a(bcd_to_7_segment_decoder_3_p6),
    .b(bcd_to_7_segment_decoder_3_p8), .e(bcd_to_7_segment_decoder_3_p2), .d(bcd_to_7_segment_decoder_3_p4),
    .c(bcd_to_7_segment_decoder_3_p7));  // open: dp
  // BCD_to_7_Segment_decoder bcd_to_7_segment_decoder_3: pin names not known; wires that end beside it: bcd_to_7_segment_decoder_3_p1, bcd_to_7_segment_decoder_3_p2, bcd_to_7_segment_decoder_3_p3, bcd_to_7_segment_decoder_3_p4, binary_to_bcd_converter_1_p4, bcd_to_7_segment_decoder_3_p6, bcd_to_7_segment_decoder_3_p7, bcd_to_7_segment_decoder_3_p8
  // Switch #(.width(8)) switch_1: pin names not known; wires that end beside it: {out_27, out_26, out_25, out_24, out_23, out_22, out_21, out_20}, binary_to_bcd_converter_1_p1

  // Notes on the sheet:
  //   000 = SOMA 
  //   010 = AND
  //   011 = OR
  //   100 = XOR
  //   101 = NAND
  //   110 = NOR 
  //   111 = XNOR
  //   ESCOLHA AS OPERAÇÕES AQUI
  //   TABELA DE OPERAÇÕES
  //   001 = SUBTRAÇÃO 
  //   DADOS DAS OPERAÇÕES DIRETAMENTE EM BINÁRIO
  //   Para mostrar o valor exato da subtração, certifique-se de colocar o maior valor na entrada A e o menor valor na entrada B 
  //   <-- LIGUE O DISPLAY AQUI
endmodule

module DiagramaHalfAdder (
  input  A,
  input  B,
  output S,
  output C0
);

  xor xor_1 (S, A, B);
  and and_1 (C0, A, B);
endmodule

module DiagramaFullAdder (
  input  Ci,
  input  A,
  input  B,
  output S,
  output C0
);

  wire diagramahalfadder_1_c0, diagramahalfadder_1_s, diagramahalfadder_2_c0;

  DiagramaHalfAdder diagramahalfadder_1 (.A(A), .B(B), .S(diagramahalfadder_1_s), .C0(diagramahalfadder_1_c0));
  DiagramaHalfAdder diagramahalfadder_2 (.A(Ci), .B(diagramahalfadder_1_s), .S(S), .C0(diagramahalfadder_2_c0));
  or or_1 (C0, diagramahalfadder_2_c0, diagramahalfadder_1_c0);
endmodule

module DiagramaFullAdder4bit (
  input  in_1,
  input  A0,
  input  B0,
  input  A1,
  input  B1,
  input  A2,
  input  B2,
  input  A3,
  input  B3,
  output S0,
  output S1,
  output S2,
  output S3,
  output C4
);

  wire diagramafulladder_1_c0, diagramafulladder_2_c0, diagramafulladder_3_c0;

  DiagramaFullAdder diagramafulladder_1 (.Ci(in_1), .A(A0), .B(B0), .S(S0), .C0(diagramafulladder_1_c0));
  DiagramaFullAdder diagramafulladder_2 (
    .Ci(diagramafulladder_1_c0), .A(A1), .B(B1), .S(S1), .C0(diagramafulladder_2_c0));
  DiagramaFullAdder diagramafulladder_3 (
    .Ci(diagramafulladder_2_c0), .A(A2), .B(B2), .S(S2), .C0(diagramafulladder_3_c0));
  DiagramaFullAdder diagramafulladder_4 (.Ci(diagramafulladder_3_c0), .A(A3), .B(B3), .S(S3), .C0(C4));
endmodule

module DiagramaFullAdder8bit (
  input  C0,
  input  A0,
  input  B0,
  input  A1,
  input  B1,
  input  A2,
  input  B2,
  input  A3,
  input  B3,
  input  A4,
  input  B4,
  input  A5,
  input  B5,
  input  A6,
  input  B6,
  input  A7,
  input  B7,
  output S0,
  output S1,
  output S2,
  output S3,
  output S4,
  output S5,
  output S6,
  output S7,
  output C8
);

  wire diagramafulladder4bit_1_c4;

  DiagramaFullAdder4bit diagramafulladder4bit_1 (
    .in_1(C0), .A0(A0), .B0(B0), .A1(A1), .B1(B1), .A2(A2), .B2(B2), .A3(A3), .B3(B3), .S0(S0), .S1(S1),
    .S2(S2), .S3(S3), .C4(diagramafulladder4bit_1_c4));
  DiagramaFullAdder4bit diagramafulladder4bit_2 (
    .in_1(diagramafulladder4bit_1_c4), .A0(A4), .B0(B4), .A1(A5), .B1(B5), .A2(A6), .B2(B6), .A3(A7),
    .B3(B7), .S0(S4), .S1(S5), .S2(S6), .S3(S7), .C4(C8));
endmodule

module FullAdder8bit (
  input  A0,
  input  B0,
  input  A1,
  input  B1,
  input  A2,
  input  B2,
  input  A3,
  input  B3,
  input  A4,
  input  B4,
  input  A5,
  input  B5,
  input  A6,
  input  B6,
  input  A7,
  input  B7,
  output S0,
  output S1,
  output S2,
  output S3,
  output S4,
  output S5,
  output S6,
  output S7,
  output Carry,
  output OVERFLOW
);

  wire xor_1_out, xor_2_out, xor_3_out, xor_4_out, xor_5_out, xor_6_out, xor_7_out, xor_8_out;

  xor xor_1 (xor_1_out, 1'b0, B6);
  xor xor_2 (xor_2_out, 1'b0, B7);
  xor xor_3 (xor_3_out, 1'b0, B5);
  xor xor_4 (xor_4_out, 1'b0, B4);
  xor xor_5 (xor_5_out, 1'b0, B2);
  xor xor_6 (xor_6_out, 1'b0, B3);
  xor xor_7 (xor_7_out, 1'b0, B1);
  xor xor_8 (xor_8_out, 1'b0, B0);
  DiagramaFullAdder8bit diagramafulladder8bit_1 (
    .C0(1'b0), .A0(A0), .B0(xor_8_out), .A1(A1), .B1(xor_7_out), .A2(A2), .B2(xor_5_out), .A3(A3),
    .B3(xor_6_out), .A4(A4), .B4(xor_4_out), .A5(A5), .B5(xor_3_out), .A6(A6), .B6(xor_1_out), .A7(A7),
    .B7(xor_2_out), .S0(S0), .S1(S1), .S2(S2), .S3(S3), .S4(S4), .S5(S5), .S6(S6), .S7(S7), .C8(Carry));
  xor xor_9 (OVERFLOW, S6, S7);

  // Notes on the sheet:
  //   SUBTRADOR A PARTIR DE UM SOMADOR DE 8 BITS
endmodule

module FullSubtractor8bit (
  input  A0,
  input  B0,
  input  A1,
  input  B1,
  input  A2,
  input  B2,
  input  A3,
  input  B3,
  input  A4,
  input  B4,
  input  A5,
  input  B5,
  input  A6,
  input  B6,
  input  A7,
  input  B7,
  output S0,
  output S1,
  output S2,
  output S3,
  output S4,
  output S5,
  output S6,
  output S7,
  output Carry,
  output OVERFLOW
);

  wire xor_1_out, xor_2_out, xor_3_out, xor_4_out, xor_5_out, xor_6_out, xor_7_out, xor_8_out;

  xor xor_1 (xor_1_out, 1'b1, B6);
  xor xor_2 (xor_2_out, 1'b1, B7);
  xor xor_3 (xor_3_out, 1'b1, B5);
  xor xor_4 (xor_4_out, 1'b1, B3);
  xor xor_5 (xor_5_out, 1'b1, B4);
  xor xor_6 (xor_6_out, 1'b1, B2);
  xor xor_7 (xor_7_out, 1'b1, B0);
  xor xor_8 (xor_8_out, 1'b1, B1);
  DiagramaFullAdder8bit diagramafulladder8bit_1 (
    .C0(1'b1), .A0(A0), .B0(xor_7_out), .A1(A1), .B1(xor_8_out), .A2(A2), .B2(xor_6_out), .A3(A3),
    .B3(xor_4_out), .A4(A4), .B4(xor_5_out), .A5(A5), .B5(xor_3_out), .A6(A6), .B6(xor_1_out), .A7(A7),
    .B7(xor_2_out), .S0(S0), .S1(S1), .S2(S2), .S3(S3), .S4(S4), .S5(S5), .S6(S6), .S7(S7), .C8(Carry));
  xor xor_9 (OVERFLOW, S6, S7);

  // Notes on the sheet:
  //   SUBTRADOR A PARTIR DE UM SOMADOR DE 8 BITS
endmodule

module AND8bitWISE (
  input  A0,
  input  B0,
  input  A1,
  input  B1,
  input  A2,
  input  B2,
  input  A3,
  input  B3,
  input  A4,
  input  B4,
  input  A5,
  input  B5,
  input  A6,
  input  B6,
  input  A7,
  input  B7,
  output S0,
  output S1,
  output S2,
  output S3,
  output S4,
  output S5,
  output S6,
  output S7
);

  and and_1 (S0, A0, B0);
  and and_2 (S1, A1, B1);
  and and_3 (S2, A2, B2);
  and and_4 (S3, A3, B3);
  and and_5 (S4, A4, B4);
  and and_6 (S5, A5, B5);
  and and_7 (S6, A6, B6);
  and and_8 (S7, A7, B7);
endmodule

module OR8bitWISE (
  input  A0,
  input  B0,
  input  A1,
  input  B1,
  input  A2,
  input  B2,
  input  A3,
  input  B3,
  input  A4,
  input  B4,
  input  A5,
  input  B5,
  input  A6,
  input  B6,
  input  A7,
  input  B7,
  output S0,
  output S1,
  output S2,
  output S3,
  output S4,
  output S5,
  output S6,
  output S7
);

  or or_1 (S0, A0, B0);
  or or_2 (S1, A1, B1);
  or or_3 (S2, A2, B2);
  or or_4 (S3, A3, B3);
  or or_5 (S4, A4, B4);
  or or_6 (S5, A5, B5);
  or or_7 (S6, A6, B6);
  or or_8 (S7, A7, B7);
endmodule

module XOR8bitWISE (
  input  A0,
  input  B0,
  input  A1,
  input  B1,
  input  A2,
  input  B2,
  input  A3,
  input  B3,
  input  A4,
  input  B4,
  input  A5,
  input  B5,
  input  A6,
  input  B6,
  input  A7,
  input  B7,
  output S0,
  output S1,
  output S2,
  output S3,
  output S4,
  output S5,
  output S6,
  output S7
);

  xor xor_1 (S0, A0, B0);
  xor xor_2 (S1, A1, B1);
  xor xor_3 (S2, A2, B2);
  xor xor_4 (S3, A3, B3);
  xor xor_5 (S4, A4, B4);
  xor xor_6 (S5, A5, B5);
  xor xor_7 (S6, A6, B6);
  xor xor_8 (S7, A7, B7);
endmodule

module NAND8bitWISE (
  input  A0,
  input  B0,
  input  A1,
  input  B1,
  input  A2,
  input  B2,
  input  A3,
  input  B3,
  input  A4,
  input  B4,
  input  A5,
  input  B5,
  input  A6,
  input  B6,
  input  A7,
  input  B7,
  output S0,
  output S1,
  output S2,
  output S3,
  output S4,
  output S5,
  output S6,
  output S7
);

  nand nand_1 (S0, A0, B0);
  nand nand_2 (S1, A1, B1);
  nand nand_3 (S2, A2, B2);
  nand nand_4 (S3, A3, B3);
  nand nand_5 (S4, A4, B4);
  nand nand_6 (S5, A5, B5);
  nand nand_7 (S6, A6, B6);
  nand nand_8 (S7, A7, B7);
endmodule

module NOR8bitWISE (
  input  A0,
  input  B0,
  input  A1,
  input  B1,
  input  A2,
  input  B2,
  input  A3,
  input  B3,
  input  A4,
  input  B4,
  input  A5,
  input  B5,
  input  A6,
  input  B6,
  input  A7,
  input  B7,
  output S0,
  output S1,
  output S2,
  output S3,
  output S4,
  output S5,
  output S6,
  output S7
);

  nor nor_1 (S0, A0, B0);
  nor nor_2 (S1, A1, B1);
  nor nor_3 (S2, A2, B2);
  nor nor_4 (S3, A3, B3);
  nor nor_5 (S4, A4, B4);
  nor nor_6 (S5, A5, B5);
  nor nor_7 (S6, A6, B6);
  nor nor_8 (S7, A7, B7);
endmodule

module XNOR8bitWISE (
  input  A0,
  input  B0,
  input  A1,
  input  B1,
  input  A2,
  input  B2,
  input  A3,
  input  B3,
  input  A4,
  input  B4,
  input  A5,
  input  B5,
  input  A6,
  input  B6,
  input  A7,
  input  B7,
  output S0,
  output S1,
  output S2,
  output S3,
  output S4,
  output S5,
  output S6,
  output S7
);

  wire xor_1_out, xor_2_out, xor_3_out, xor_4_out, xor_5_out, xor_6_out, xor_7_out, xor_8_out;

  xor xor_1 (xor_1_out, A0, B0);
  not not_1 (S0, xor_1_out);
  xor xor_2 (xor_2_out, A1, B1);
  not not_2 (S1, xor_2_out);
  xor xor_3 (xor_3_out, A2, B2);
  not not_3 (S2, xor_3_out);
  xor xor_4 (xor_4_out, A3, B3);
  not not_4 (S3, xor_4_out);
  xor xor_5 (xor_5_out, A4, B4);
  not not_5 (S4, xor_5_out);
  xor xor_6 (xor_6_out, A5, B5);
  not not_6 (S5, xor_6_out);
  xor xor_7 (xor_7_out, A6, B6);
  not not_7 (S6, xor_7_out);
  xor xor_8 (xor_8_out, A7, B7);
  not not_8 (S7, xor_8_out);
endmodule
