// Logisim project somador_4bit_sem_Hierarquia.circ as structural Verilog: 1 circuit, main circuit SOMADOR4BIT
module SOMADOR4BIT (
  input  B3,
  input  A3,
  input  B2,
  input  A2,
  input  B1,
  input  A1,
  input  B0,
  input  A0,
  output S0,
  output S1,
  output S2,
  output S3,
  output C4
);

  wire and_1_out, and_2_out, and_3_out, and_4_out, and_5_out, and_6_out, and_7_out, and_8_out, and_9_out,
       and_10_out, or_1_out, or_2_out;

  xor xor_1 (S0, B0, A0);
  and and_1 (and_1_out, B0, A0);
  LED led_1 (.in(S0));
  and and_2 (and_2_out, and_1_out, A1);
  and and_3 (and_3_out, and_1_out, B1);
  and and_4 (and_4_out, A1, B1);
  ExactlyOne xor_2 (.out(S1), .in0(and_1_out), .in1(A1), .in2(B1));
  or or_1 (or_1_out, and_2_out, and_3_out, and_4_out);
  LED led_2 (.in(S1));
  and and_5 (and_5_out, or_1_out, A2);
  and and_6 (and_6_out, or_1_out, B2);
  and and_7 (and_7_out, A2, B2);
  LED led_3 (.in(S2));
  ExactlyOne xor_3 (.out(S2), .in0(or_1_out), .in1(A2), .in2(B2));
  or or_2 (or_2_out, and_5_out, and_6_out, and_7_out);
  and and_8 (and_8_out, or_2_out, A3);
  and and_9 (and_9_out, or_2_out, B3);
  and and_10 (and_10_out, A3, B3);
  LED led_4 (.in(S3));
  ExactlyOne xor_4 (.out(S3), .in0(or_2_out), .in1(A3), .in2(B3));
  or or_3 (C4, and_8_out, and_9_out, and_10_out);
  LED led_5 (.in(C4));

  // Notes on the sheet:
  //   SOMADOR DE 4 BITS SEM HIERARQUIA DE CIRCUITOS
  //   OVERFLOW  DE 4 BIT
endmodule
