// Logisim project subtrador_com_somadores.circ as structural Verilog: 4 circuits, main circuit halfSUBTRACTOR
module halfSUBTRACTOR (
  input  A0,
  input  B0,
  output S,
  output C0
);

  xor xor_1 (S, A0, B0);
  and and_1 (C0, A0, B0);
endmodule

module FULLADDER1BIT (
  input  Ti,
  input  A0,
  input  B0,
  output S,
  output T0
);

  wire halfsubtractor_1_c0, halfsubtractor_1_s, halfsubtractor_2_c0;

  halfSUBTRACTOR halfsubtractor_1 (.A0(A0), .B0(B0), .S(halfsubtractor_1_s), .C0(halfsubtractor_1_c0));
  halfSUBTRACTOR halfsubtractor_2 (.A0(Ti), .B0(halfsubtractor_1_s), .S(S), .C0(halfsubtractor_2_c0));
  or or_1 (T0, halfsubtractor_2_c0, halfsubtractor_1_c0);
endmodule

module FULLADDER4BIT (
  input  M,
  input  A0,
  input  B0,
  input  A1,
  input  B1,
  input  A2,
  input  B2,
  input  A3,
  input  B3,
  output S0,
  output S1,
  output S2,
  output S3,
  output C4
);

  wire fulladder1bit_1_t0, fulladder1bit_2_t0, fulladder1bit_3_t0;

  FULLADDER1BIT fulladder1bit_1 (.Ti(M), .A0(A0), .B0(B0), .S(S0), .T0(fulladder1bit_1_t0));
  FULLADDER1BIT fulladder1bit_2 (.Ti(fulladder1bit_1_t0), .A0(A1), .B0(B1), .S(S1), .T0(fulladder1bit_2_t0));
  FULLADDER1BIT fulladder1bit_3 (.Ti(fulladder1bit_2_t0), .A0(A2), .B0(B2), .S(S2), .T0(fulladder1bit_3_t0));
  FULLADDER1BIT fulladder1bit_4 (.Ti(fulladder1bit_3_t0), .A0(A3), .B0(B3), .S(S3), .T0(C4));
endmodule

module FULLSUBSTRACTOR8BIT (
  input  CONTROLADOR,
  input  A0,
  input  B0,
  input  A1,
  input  B1,
  input  A2,
  input  B2,
  input  A3,
  input  B3,
  input  A4,
  input  B4,
  input  A5,
  input  B5,
  input  A6,
  input  B6,
  input  A7,
  input  B7,
  output S0,
  output S1,
  output S2,
  output S3,
  output S4,
  output S5,
  output S6,
  output S7,
  output out_26
);

  wire fulladder4bit_1_c4, xor_1_out, xor_2_out, xor_3_out, xor_4_out, xor_5_out, xor_6_out, xor_7_out,
       xor_8_out;

  xor xor_1 (xor_1_out, CONTROLADOR, B0);
  xor xor_2 (xor_2_out, CONTROLADOR, B1);
  xor xor_3 (xor_3_out, CONTROLADOR, B2);
  xor xor_4 (xor_4_out, CONTROLADOR, B3);
  xor xor_5 (xor_5_out, CONTROLADOR, B4);
  xor xor_6 (xor_6_out, CONTROLADOR, B5);
  xor xor_7 (xor_7_out, CONTROLADOR, B6);
  xor xor_8 (xor_8_out, CONTROLADOR, B7);
  FULLADDER4BIT fulladder4bit_1 (
    .M(CONTROLADOR), .A0(A0), .B0(xor_1_out), .A1(A1), .B1(xor_2_out), .A2(A2), .B2(xor_3_out), .A3(A3),
    .B3(xor_4_out), .S0(S0), .S1(S1), .S2(S2), .S3(S3), .C4(fulladder4bit_1_c4));
  FULLADDER4BIT fulladder4bit_2 (
    .M(fulladder4bit_1_c4), .A0(A4), .B0(xor_5_out), .A1(A5), .B1(xor_6_out), .A2(A6), .B2(xor_7_out),
    .A3(A7), .B3(xor_8_out), .S0(S4), .S1(S5), .S2(S6), .S3(S7), .C4(out_26));
  LED C8 (.in(out_26));
  LED led_1 (.in(S0));
  LED led_2 (.in(S1));
  LED led_3 (.in(S2));
  LED led_4 (.in(S3));
  LED led_5 (.in(S4));
  LED led_6 (.in(S5));
  LED led_7 (.in(S6));
  LED led_8 (.in(S7));

  // Notes on the sheet:
  //   PREFERI ADICIONAR AS XOR COM O MEU CONTROLADOR DIRETO NO MEU SUBSTRACTOR, PARA ESPECIFICAR A DIFERENÇA
endmodule
